# Fritzing sketch FSR (saved by Fritzing 0.9.0b)
circuit board: 7.09241cm x 2.52113cm
breadboards: 1

parts:
  Spark_Core = Spark Core (v1.0)
  Rm = Resistor [tolerance=±5% resistance=10k package=THT]
  U1 = LM 358 Dual Op-Amp [package="DIP8 [THT]"]  # not connected
  Bend = Basic Flex Resistor

nets:
  N1: Spark_Core.A0, Rm.Pin_1, Bend.Pin_2
  N2: Spark_Core.GND, Rm.Pin_0
  N3: Spark_Core.3V3*, Bend.pin_1
