# Fritzing sketch SparkFSR (saved by Fritzing 0.9.0b)
circuit board: 8.46667cm x 5.64444cm
breadboards: 1

parts:
  FSR = Basic Force Sensing Resistor (FSR) [package=THT]
  Spark_Core = Spark Core (v1.0)

nets:
  N1: FSR.pin_0, Spark_Core.A6
  N2: FSR.pin_1, Spark_Core.3V3*

notes:
  Enable pull-down resistor in Spark code.
